# Fritzing sketch santaCatch-FRITZING_circuit (saved by Fritzing 0.9.3b)
circuit board: 2.29257cm x 1.3299cm

parts:
  PIRSensor1 = HC-SR501 Body Sensor Module
  Raspberry_Pi_1 = Raspberry Pi 3 [part_number=RPI-3-V1.2]

nets:
  VCC: PIRSensor1.VCC, Raspberry_Pi_1.5V
  N1: PIRSensor1.OUT, Raspberry_Pi_1.GIPO4
  GND: PIRSensor1.GND, Raspberry_Pi_1.GND

custom parts:
  HC-SR501 Body Sensor Module: Pyroelectric Infrared PIR Motion Sensor Detector Module
